# Fritzing sketch PIRRGBledUNO9V (saved by Fritzing 0.9.2b)
breadboards: 1

parts:
  RGB_led = RGB LED - (4 legs) [package="5 mm [THT]"]
  BAT1 = BC9VPC [package=bc9vpc]
  Part3 = Arduino Uno (Rev3) - ICSP
  part = Resistor [tolerance=±5% resistance=330 package=THT]
  part_2 = Resistor [tolerance=±5% resistance=330 package=THT]
  part_3 = Resistor [tolerance=±5% resistance=330 package=THT]
  PIR2 = PIR sensor

nets:
  N1: RGB_led.red_cathode, part_3.Pin_0
  5V: RGB_led.common_anode, Part3.5V, PIR2.VCC
  N2: RGB_led.green_cathode, part_2.Pin_0
  N3: RGB_led.blue_cathode, part.Pin_0
  N4: BAT1.V+, Part3.VIN
  GND: BAT1.V-, Part3.GND, PIR2.GND
  N5: Part3.D10_PWM/SS, PIR2.SIG
  N6: Part3.D3_PWM, part.Pin_1
  N7: Part3.D5_PWM, part_2.Pin_1
  N8: Part3.D6_PWM, part_3.Pin_1
